# Fritzing sketch proyectoPrueba00 (saved by Fritzing 0.9.3b)
breadboards: 1

parts:
  Componente1 = Arduino Uno (Rev3) - ICSP
  LCD1 = LCD screen
  Componente2 = Adafruit I2C+SPI LCD Backpack [part_number="Adafruit #292"]
  S1 = Round Pushbutton
  R1 = Resistor [tolerance=±5% resistance=220 package=THT]

nets:
  GND: Componente1.GND, LCD1.VSS, LCD1.R/W, Componente2.GND, S1.leg1
  5V: Componente1.5V, LCD1.VDD, LCD1.LED+, Componente2.VCC
  N1: LCD1.V0, Componente2.CONTRAST
  N2: LCD1.RS, Componente2.RS
  N3: LCD1.E, Componente2.E
  N4: LCD1.DB0, Componente2.DB0
  N5: LCD1.DB1, Componente2.DB1
  N6: LCD1.DB2, Componente2.DB2
  N7: LCD1.DB3, Componente2.DB3
  N8: LCD1.DB4, Componente2.DB4
  N9: LCD1.DB5, Componente2.DB5
  N10: LCD1.DB6, Componente2.DB6
  N11: LCD1.DB7, Componente2.DB7
  N12: LCD1.LED-, Componente2.LEDK
  N13: S1.leg0, R1.Pin_1

custom parts:
  Adafruit I2C+SPI LCD Backpack: LCD backpacks reduce the number of pins needed to connect to an LCD. LCDs are a fun and easy way to have your microcontroller project talk back to you. Character LCDs are common, and easy to get, available in tons of colors and sizes. We've written tutorials on using character LCDs with an Arduino (or similar microcontroller) but find that the number of pins necessary to control the LCD can be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
